# Fritzing sketch Sketch (saved by Fritzing 1.0.5)
breadboards: 2

parts:
  M1 = DOIT Esp32 DevKit v1 (30 pins long, 11 pins width) [part_number=ESP32S-PIN30]
  J1 = Piezo Speaker
  R1 = Resistor [tolerance=±5% resistance=220 package="2010 [SMD]"]
  R2 = Resistor [tolerance=±5% resistance=1 package="2010 [SMD]"]
  MOSFET1 = Basic FET N-Channel [package="TO220 [THT]"]
  FC-1 = Sound Sensor
  DHT1 = Humidity and Temperature Sensor DHT11
  S1 = MC-38  # not connected
  JACK1 = 2.1mm Barrel Jack with Terminal Block
  BAT1 = Battery Holders [package=battery-aa-kit]  # not connected
  JACK2 = 2.1mm Barrel Jack with Terminal Block
  LED1 = LEDs [package=led10mm]  # not connected

nets:
  VCC: M1.3V3, FC-1.VCC, DHT1.Vcc
  GND: M1.GND, J1.pin1, R1.Pin_0, MOSFET1.source, FC-1.GND, DHT1.GND_2, JACK1.NEG
  N1: M1.D4, DHT1.Data-signal
  N2: M1.D34, FC-1.OUT
  N3: M1.D35, R1.Pin_1
  N4: M1.D33, R2.Pin_0
  N5: M1.D25, J1.pin2
  N6: R2.Pin_1, MOSFET1.gate
  N7: MOSFET1.drain, JACK2.NEG
  N8: JACK1.POS, JACK2.POS

custom parts:
  DOIT Esp32 DevKit v1 (30 pins long, 11 pins width): The DOIT Esp32 DevKit v1 is one of the development board created by DOIT to evaluate the ESP-WROOM-32 module. It is based on the ESP32 microcontroller that boasts Wifi, Bluetooth, Ethernet and Low Power support all in a single chip. (vanepp) made breadboard work, adjusted pin numbering and labels and reduced size of schematic and cleaned up pcb. This chip is 30pins long (2 x15) and 11 pins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
  Humidity and Temperature Sensor DHT11: Digital relative humidity & temperature sensor DHT11
  MC-38: MC-38 Contact Sensor w/ Reed Switch
